# Fritzing sketch PowerManual (saved by Fritzing 0.9.9b)
breadboards: 2

parts:
  LED2 = RGB LED (com. cathode, rgb) [package="5 mm [THT]"]
  MCU = Arduino Nano (Rev3.0)
  Sensor = InvenSense MPU6050
  S1 = Toggle Switch [package=THT]
  LED1 = smd LED [color="Green (555nm)" package="0603 [SMD]"]
  R1 = Resistor [tolerance=±5% power=0.25 resistance=220 package=THT]
  R2 = Resistor [tolerance=±5% power=0.25 resistance=220 package=THT]
  R3 = Resistor [tolerance=±5% power=0.25 resistance=220 package=THT]
  R4 = Resistor [tolerance=±5% power=0.25 resistance=220 package=THT]
  LED3 = RGB LED (com. cathode, rgb) [package="5 mm [THT]"]
  R5 = Resistor [tolerance=±5% power=0.25 resistance=220 package=THT]
  R7 = Resistor [tolerance=±5% power=0.25 resistance=220 package=THT]
  R6 = Resistor [tolerance=±5% power=0.25 resistance=220 package=THT]
  TP = TP4056 [chip_label=TP4056 package="DIP (Dual Inline) [THT]"]
  BAT = Battery Holders [package=battcom_20mm_pth]
  BT = Bluetooth HC-06u [package=THT]
  S2 = Pushbutton horitzontal [package=THT]

nets:
  N1: LED2.red_anode, R4.Pin_1
  GND: LED2.common_cathode, MCU.GND, Sensor.GND, LED1.cathode, LED3.common_cathode, TP.pin6, BT.GND, S2.pin_1
  N2: LED2.green_anode, R3.Pin_0
  N3: LED2.blue_anode, R2.Pin_0
  N4: MCU.D2, BT.TXD
  N5: MCU.D3, BT.RXD
  N6: MCU.D4, S2.pin_0
  N7: MCU.D5, R1.Pin_1
  N8: MCU.D6, R2.Pin_1
  N9: MCU.D7, R3.Pin_1
  N10: MCU.D8, R4.Pin_0
  N11: MCU.D9, R7.Pin_0
  N12: MCU.D10, LED3.green_anode, R6.Pin_1
  N13: MCU.D11/MOSI, R5.Pin_1
  VCC: MCU.VIN, Sensor.VCC, S1.L2, BT.VCC
  N14: MCU.A5, Sensor.SCL
  N15: MCU.A4, Sensor.SDA
  N16: S1.COM, TP.pin3
  N17: LED1.anode, R1.Pin_0
  N18: LED3.red_anode, R5.Pin_0
  N19: LED3.blue_anode, R7.Pin_1
  N20: TP.pin4, BAT.+
  N21: TP.pin5, BAT.-

custom parts:
  TP4056: A DIP stand-in part for whatever IC you want. With 6 pins on a 300mil dual inline package (DIP) footprint.
  Bluetooth HC-06u: Bluetooth HC-06 - face up, pins down 16.5mm x 37.5mm PCB
  Pushbutton horitzontal: A generic pushbutton with horizontal button orientation.
