# Fritzing sketch PowerManualDevice (saved by Fritzing 0.9.9b)

parts:
  MCU1 = Arduino Nano (Rev3.0)
  Sensor1 = InvenSense MPU6050
  S2 = Toggle Switch [package=THT]
  R8 = Resistor [tolerance=±5% power=0.25 resistance=220 package=THT]
  R9 = Resistor [tolerance=±5% power=0.25 resistance=220 package=THT]
  R10 = Resistor [tolerance=±5% power=0.25 resistance=220 package=THT]
  LED4 = RGB LED (com. cathode, rgb) [package="5 mm [THT]"]
  TP1 = TP4056 [chip_label=TP4056 package="DIP (Dual Inline) [THT]"]
  BAT1 = Battery Holders [package=battcom_20mm_pth]
  BT1 = Bluetooth HC-06u [package=THT]

nets:
  N1: MCU1.D2, BT1.TXD
  N2: MCU1.D3, BT1.RXD
  N3: MCU1.D9, R9.Pin_0
  N4: MCU1.D10, R10.Pin_0
  N5: MCU1.D11/MOSI, R8.Pin_0
  N6: MCU1.VIN, S2.L1
  GND: MCU1.GND, Sensor1.GND, LED4.common_cathode, TP1.pin6, BT1.GND
  N7: MCU1.A5, Sensor1.SCL
  N8: MCU1.A4, Sensor1.SDA
  VCC: MCU1.3V3, Sensor1.VCC, BT1.VCC
  N9: S2.COM, TP1.pin3
  N10: TP1.pin4, BAT1.+
  N11: TP1.pin5, BAT1.-

custom parts:
  TP4056: A DIP stand-in part for whatever IC you want. With 6 pins on a 300mil dual inline package (DIP) footprint.
  Bluetooth HC-06u: Bluetooth HC-06 - face up, pins down 16.5mm x 37.5mm PCB
